# Fritzing sketch clocksilencer (saved by Fritzing 0.9.10b)
breadboards: 1

parts:
  BAT1 = 18650 battery holder [package=battery-18650-kit]
  U1 = ESP32-38PinWide [part_number=ESP32-38PinWide]
  SP1 = SPEAKER [package=pcb_mount_speaker]
  DFPlayer_Mini1 = DFPlayer MINI [package="DIP (Dual Inline) [THT]"]
  Q1 = Basic FET N-Channel [package="TO220 [THT]"]
  U2 = V_REG_LD1117VXX [package=78xxl]

nets:
  GND: BAT1.+, U1.GND, Q1.source, U2.GND
  N1: BAT1.-, DFPlayer_Mini1.VCC, U2.IN
  N2: U1.3.3, U2.OUT
  N3: U1.GPIO14, Q1.gate
  N4: U1.GPIO3, DFPlayer_Mini1.TX
  N5: U1.GPIO1, DFPlayer_Mini1.RX
  N6: SP1.+, DFPlayer_Mini1.SPK1
  N7: SP1.-, DFPlayer_Mini1.SPK2
  N8: DFPlayer_Mini1.GND, Q1.drain

notes:
  N-mosfet for DFPlayer Mini
  Voltage regulator (3.3 V)

custom parts:
  18650 battery holder: 18650 Battery Holder identical to the dual battery version.
  ESP32-38PinWide: Generic 38-Pin ESP32 with wide format (only access to one side of pins on a breadboard) based on Stephen Lilley's HiLetgo ESP-WROOM-32 ESP32 ESP-32S Development Board.
  DFPlayer MINI: MP3 module by DFRobot.com for playing Music from an SD-Card. Supports WAV and MP3 files.
